# Fritzing sketch 5-1 (saved by Fritzing 0.9.4)
breadboards: 1

parts:
  DI1 = 7-Segment LED Display [package=THT]
  R1 = Resistor [tolerance=±5% resistance=220 package=THT]
  R2 = Resistor [tolerance=±5% resistance=220 package=THT]
  R3 = Resistor [tolerance=±5% resistance=220 package=THT]
  R4 = Resistor [tolerance=±5% resistance=220 package=THT]
  R5 = Resistor [tolerance=±5% resistance=220 package=THT]
  R6 = Resistor [tolerance=±5% resistance=220 package=THT]
  R7 = Resistor [tolerance=±5% resistance=220 package=THT]
  Part1 = Arduino Uno (Rev3)

nets:
  N1: DI1.cathodeE, R7.Pin_1
  N2: DI1.cathodeD, R6.Pin_1
  N3: DI1.commAnode#2, Part1.GND
  N4: DI1.cathodeC, R5.Pin_0
  N5: DI1.cathodeB, R1.Pin_0
  N6: DI1.cathodeA, R2.Pin_0
  N7: DI1.cathodeF, R3.Pin_1
  N8: DI1.cathodeG, R4.Pin_1
  N9: R1.Pin_1, Part1.D1/TX
  N10: R2.Pin_1, Part1.D2
  N11: R3.Pin_0, Part1.D6_PWM
  N12: R4.Pin_0, Part1.D7
  N13: R5.Pin_1, Part1.D3_PWM
  N14: R6.Pin_0, Part1.D4
  N15: R7.Pin_0, Part1.D5_PWM
