# Fritzing sketch 5-3 (saved by Fritzing 0.9.4)
breadboards: 1

parts:
  R1 = Photocell (LDR) [package=THT]
  LED1 = LED - 5mm [color="Red (633nm)" package="5 mm [THT]"]
  Part1 = Arduino Uno (Rev3)
  R2 = Resistor [tolerance=±5% resistance=220 package=THT]

nets:
  N1: R1.pin_0, Part1.5V
  N2: R1.pin_1, Part1.A0, R2.Pin_0
  N3: LED1.cathode, Part1.D13/SCK
  N4: LED1.anode, Part1.GND, R2.Pin_1
