# Fritzing sketch 5-4 (saved by Fritzing 0.9.4)
breadboards: 1

parts:
  S1 = Pushbutton [package="[THT]"]
  S2 = Pushbutton [package="[THT]"]
  S3 = Pushbutton [package="[THT]"]
  S4 = Pushbutton [package="[THT]"]
  Part1 = Arduino Uno (Rev3)
  SP1 = SPEAKER [package=pcb_mount_speaker]

nets:
  N1: S1.Pin_1, S1.Pin_2, S2.Pin_1, S2.Pin_2, S3.Pin_1, S3.Pin_2, S4.Pin_1, S4.Pin_2, Part1.GND, SP1.+
  N2: S1.Pin_3, S1.Pin_4, Part1.D8
  N3: S2.Pin_3, S2.Pin_4, Part1.D7
  N4: S3.Pin_3, S3.Pin_4, Part1.D6_PWM
  N5: S4.Pin_3, S4.Pin_4, Part1.D5_PWM
  N6: Part1.D11_PWM/MOSI, SP1.-
