# Fritzing sketch 5-5 (saved by Fritzing 0.9.4)
breadboards: 1

parts:
  DHT1 = DHT11 Humitidy and Temperature Sensor (3 pins)
  LED1 = LED - 5mm [color="Red (633nm)" package="5 mm [THT]"]
  LED2 = LED - 5mm [color="Red (633nm)" package="5 mm [THT]"]
  R1 = Resistor [tolerance=±5% resistance=220 package=THT]
  Part1 = Arduino Uno (Rev3)

nets:
  N1: DHT1.Plus, R1.Pin_0, Part1.5V
  N2: DHT1.Signal, R1.Pin_1, Part1.D8
  GND: DHT1.Gnd, LED1.anode, LED2.anode, Part1.GND
  N3: LED1.cathode, Part1.D7
  N4: LED2.cathode, Part1.D6_PWM

custom parts:
  DHT11 Humitidy and Temperature Sensor (3 pins): DHT11 Humidity and Temperature Sensor (3 pins).
